# Fritzing sketch Antenna Amplifier (saved by Fritzing 0.9.6b)
circuit board: 6.48533cm x 2.99203cm
breadboards: 1

parts:
  2N3904 = NPN-Transistor [package="TO92 [THT]"]
  200R = Resistor [tolerance=±5% power=0.25 resistance=200 package=THT]
  1nF = Ceramic Capacitor [capacitance=1nF voltage=35V package="100 mil [THT, multilayer]"]
  ANTENNA = Inductor [package="400 mil [THT]"]
  4_7K = Resistor [tolerance=±5% power=0.25 resistance=4.7k package=THT]
  100R = Resistor [tolerance=±5% power=0.25 resistance=50 package=THT]
  39 = Raspberry Pi Zero
  VCC_5V_/_3V3 = Toggle Switch [package=THT]
  100R_2 = Resistor [tolerance=±5% power=0.25 resistance=0 package=THT]
  SHUTDOWN = Pushbutton [package=THT]

nets:
  N1: 2N3904.E, ANTENNA.pin_1, 39.pin_6, 39.pin_9, 39.pin_20, 39.pin_25, 39.pin_39, SHUTDOWN.leg1
  N2: 2N3904.B, 4_7K.Pin_1, 100R.Pin_1, 100R_2.Pin_1
  N3: 2N3904.C, 200R.Pin_1, 1nF.0
  N4: 200R.Pin_0, VCC_5V_/_3V3.COM
  N5: 1nF.1, ANTENNA.pin_0
  N6: 4_7K.Pin_0, 39.pin_7
  N7: 100R.Pin_0, 39.pin_11, 100R_2.Pin_0
  N8: 39.pin_1, VCC_5V_/_3V3.L2
  N9: 39.pin_2, VCC_5V_/_3V3.L1
  N10: 39.pin_5, SHUTDOWN.leg0

notes:
  Antenna Amp
  github.com/hzeller/txtempus
  1
  2
  40
  Circuit: Andreas Spiess (youtu.be/6SHGAEhnsYk)
  PCB: github.com/GOTO-GOSUB
