# Fritzing sketch Compact Antenna Amplifier (saved by Fritzing 0.9.6b)
circuit board: 2.48965cm x 2.10005cm
breadboards: 1

parts:
  2N3904 = NPN-Transistor [package="TO92 [THT]"]
  200R = Resistor [tolerance=±5% power=0.25 resistance=200 package=THT]
  1nF = Ceramic Capacitor [capacitance=1nF voltage=35V package="100 mil [THT, multilayer]"]
  ANTENNA = Inductor [package="400 mil [THT]"]
  4_7K = Resistor [tolerance=±5% power=0.25 resistance=4.7k package=THT]
  100R = Resistor [tolerance=±5% power=0.25 resistance=50 package=THT]
  3V3_/_5V = Toggle Switch [package=THT]
  100R_2 = Resistor [tolerance=±5% power=0.25 resistance=0 package=THT]
  SDOWN = Pushbutton [package=THT]
  PI = Raspberry Pi Zero

nets:
  N1: 2N3904.E, ANTENNA.pin_1, SDOWN.leg1, PI.pin_6, PI.pin_9, PI.pin_20, PI.pin_39
  N2: 2N3904.B, 4_7K.Pin_1, 100R.Pin_1, 100R_2.Pin_1
  N3: 2N3904.C, 200R.Pin_1, 1nF.0
  N4: 200R.Pin_0, 3V3_/_5V.COM
  N5: 1nF.1, ANTENNA.pin_0
  N6: 4_7K.Pin_0, PI.pin_7
  N7: 100R.Pin_0, 100R_2.Pin_0, PI.pin_11
  N8: 3V3_/_5V.L1, PI.pin_2
  N9: 3V3_/_5V.L2, PI.pin_1
  N10: SDOWN.leg0, PI.pin_5

notes:
  1
  2
  40
  GOTO-GOSUB
