# Fritzing sketch Ultra Compact SMT Amplifier (saved by Fritzing 0.9.6b)
circuit board: 2.46863cm x 1.68808cm
breadboards: 1

parts:
  ANTENNA = Inductor [package="400 mil [THT]"]
  200R = Resistor [tolerance=±5% resistance=200 power=0.25 package="1206 [SMD]"]
  4_7K = Resistor [tolerance=±5% resistance=4.7k power=0.25 package="1206 [SMD]"]
  100R = Resistor [tolerance=±5% resistance=100 power=0.25 package="1206 [SMD]"]
  2N3904 = NPN-Transistor [package="SOT-23 [SMD]"]
  1nF = Ceramic Capacitor [capacitance=1nF voltage=35V package="1206 [SMD, multilayer]"]
  100R_2 = Resistor [tolerance=±5% resistance=100 power=0.25 package="1206 [SMD]"]
  PI = Raspberry Pi Zero
  5V_/_3V3 = Toggle Switch [package=THT]

nets:
  N1: ANTENNA.pin_0, 1nF.1
  GND: ANTENNA.pin_1, 2N3904.2, PI.pin_6, PI.pin_9
  N2: 200R.Pin_0, 5V_/_3V3.COM
  N3: 200R.Pin_1, 2N3904.1, 1nF.0
  N4: 4_7K.Pin_0, PI.pin_7
  N5: 4_7K.Pin_1, 100R.Pin_1, 2N3904.0, 100R_2.Pin_1
  N6: 100R.Pin_0, 100R_2.Pin_0, PI.pin_11
  N7: PI.pin_1, 5V_/_3V3.L2
  N8: PI.pin_2, 5V_/_3V3.L1

notes:
  1
  2
  INSULATE
  UNDERSIDE
  1206
